// Digital circuit cpu.dig as structural Verilog
module cpu (
  input  clk
);

  wire AddrSelect, AssertA, AssertAlu, AssertB, Carry, JumpEnable, LoadA, LoadB, LoadIR, LoadMAR, LoadPC,
       LoadTemp;
  wire [1:0] BusAssert, RightSelect, Sequencer_out;
  wire [2:0] BusLoad;
  wire [3:0] AluOp;
  wire [7:0] add_1_s, add_2_s, AddressBus, and_1_out, B_q, DataBus, driver_1_out, IR_q, lhs, LoadMemory,
       MAR_q, multiplexer_1_out, multiplexer_4_out, not_1_out, not_2_out, or_1_out, PC_q, rhs, SHL_out,
       SHR_out, Temp_q, xor_1_out;
  wire [7:1] undriven;
  wire [8:8] undriven_2;

  Multiplexer #(.Bits(8)) multiplexer_1 (
    .sel(JumpEnable), .in_0(add_1_s), .in_1(driver_1_out), .out(multiplexer_1_out));
  Register #(.Bits(8)) PC (.D(multiplexer_1_out), .C(clk), .en(LoadPC), .Q(PC_q));
  Add #(.Bits(8)) add_1 (.a(PC_q), .b({undriven, 1'b1}), .c_i(1'b0), .s(add_1_s));  // open: c_o
  Multiplexer #(.Bits(8)) multiplexer_2 (.sel(AddrSelect), .in_0(PC_q), .in_1(MAR_q), .out(AddressBus));
  Register #(.Bits(8)) MAR (.D(driver_1_out), .C(clk), .en(LoadMAR), .Q(MAR_q));
  assign not_1_out = ~LoadMemory;  // Not not_1, 8 bits wide
  assign driver_1_out = not_1_out[0] ? DataBus : 8'bz;  // Driver driver_1
  assign DataBus = LoadMemory[0] ? driver_1_out : 8'bz;  // Driver driver_2
  assign driver_1_out[0] = AssertA ? lhs[0] : 1'bz;  // Driver driver_3
  assign driver_1_out[0] = AssertB ? B_q[0] : 1'bz;  // Driver driver_4
  assign driver_1_out[0] = AssertB ? Temp_q[0] : 1'bz;  // Driver driver_5
  Register #(.Bits(8)) A (.D(driver_1_out), .C(clk), .en(LoadA), .Q(lhs));
  Register #(.Bits(8)) B (.D(driver_1_out), .C(clk), .en(LoadB), .Q(B_q));
  Register #(.Bits(8)) Temp (.D(driver_1_out), .C(clk), .en(LoadTemp), .Q(Temp_q));
  Register #(.Bits(8)) IR (.D(driver_1_out), .C(clk), .en(LoadIR), .Q(IR_q));
  Counter #(.Bits(2)) Sequencer (.en(1'b1), .C(clk), .clr(1'b0), .out(Sequencer_out));  // open: ovf
  assign driver_1_out = AssertAlu ? multiplexer_4_out : 8'bz;  // Driver driver_6
  Multiplexer #(.Bits(8), .Selector_Bits(2)) multiplexer_3 (
    .sel(RightSelect), .in_0(B_q), .in_1(Temp_q), .in_2({3'b000, IR_q[4:0]}), .in_3(lhs), .out(rhs));
  ROM #(.AddrBits(9), .Bits(12)) Decode (
    .A({undriven_2[8], Carry, IR_q[4:0], Sequencer_out}), .sel(1'b1),
    .D({AluOp, BusAssert, BusLoad, RightSelect[0], AddrSelect, LoadPC}));
  Add #(.Bits(8)) add_2 (.a(lhs), .b(rhs), .s(add_2_s));  // open: c_i, c_o
  BarrelShifter #(.Bits(8)) SHL (.in(lhs), .shift(1'b1), .out(SHL_out));
  BarrelShifter #(.Bits(8), .direction("right")) SHR (.in(lhs), .shift(1'b1), .out(SHR_out));
  Decoder #(.Selector_Bits(3)) decoder_1 (.sel(BusLoad));  // open: out_0, out_1, out_2, out_3, out_4, out_5, out_6, out_7
  assign and_1_out = lhs & rhs;  // And and_1, 8 bits wide
  assign or_1_out = lhs | rhs;  // Or or_1, 8 bits wide
  assign xor_1_out = lhs ^ rhs;  // XOr xor_1, 8 bits wide
  assign not_2_out = ~lhs;  // Not not_2, 8 bits wide
  Multiplexer #(.Bits(8), .Selector_Bits(3)) multiplexer_4 (
    .in_0(add_2_s), .in_1(SHL_out), .in_2(SHR_out), .in_3(and_1_out), .in_4(or_1_out), .in_5(xor_1_out),
    .in_6(not_2_out), .out(multiplexer_4_out));  // open: sel, in_7
  Decoder #(.Selector_Bits(2)) decoder_2 (.sel(BusAssert));  // open: out_0, out_1, out_2, out_3
  // Pins of 1 and 8 bits meet at driver_1_out
  // Pins of 1 and 8 bits meet at lhs
  // Pins of 1 and 8 bits meet at B_q
  // Pins of 1 and 2 bits meet at RightSelect
  // Pins of 1 and 8 bits meet at Temp_q
  // Pins of 1 and 8 bits meet at {undriven, 1'b1}
  // Pins of 1 and 8 bits meet at LoadMemory
  // Pins of 1 and 8 bits meet at not_1_out
  // Pins of 5 and 8 bits meet at IR_q
  // Pins of 8 and 9 bits meet at {undriven_2[8], Carry, IR_q[4:0], Sequencer_out}
endmodule
